# Fritzing sketch airquality-sensor (saved by Fritzing 0.9.8b)
breadboards: 1

parts:
  Mod1 = Raspberry Pi Pico
  Espessif_Serial_Wifi_Modul_1 = ESP8266 ESP01 [part_number=ESP8266 package=THT]
  Onderdeel1 = Adafruit SGP30 [part_number="Adafruit #3709"]

nets:
  GND: Mod1.pin_3, Mod1.pin_8, Mod1.pin_13, Mod1.pin_18, Mod1.pin_23, Mod1.pin_28, Mod1.pin_33, Mod1.pin_38, Espessif_Serial_Wifi_Modul_1.GND, Onderdeel1.GND
  N1: Mod1.pin_6, Espessif_Serial_Wifi_Modul_1.RXD
  N2: Mod1.pin_7, Espessif_Serial_Wifi_Modul_1.TXD
  N3: Mod1.pin_11, Onderdeel1.SDA
  N4: Mod1.pin_12, Onderdeel1.SCL
  N5: Mod1.pin_36, Espessif_Serial_Wifi_Modul_1.VCC, Espessif_Serial_Wifi_Modul_1.CH_PD

notes:
  Air quality sensor, Raspberry Pico + ESP-01 + SGP30, 0.9

custom parts:
  Raspberry Pi Pico: Raspberry Pi Pico. Based around the RP2040 microcontroller the Pico is a low cost microcontroller device bringing Raspberry Pi quality, cost, and easy of use to the microcontroller space. Jan 2021, Split part in to two versions: tht (this one) and SMD. This one will drill holes for a .1 in header in pcb to allow plugging in the module as well as providing pads to solder the module to the top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
  ESP8266 ESP01: Generic WiFi Module based on the ESP8266 with onboard PCB antenna and UART communications
  Adafruit SGP30: Breathe easy with the SGP30 Multi-Pixel Gas Sensor, a fully integrated MOX gas sensor. This is a very fine air quality sensor from the sensor experts at Sensirion, with I2C interfacing and fully calibrated output signals with a typical accuracy of 15% within measured values. The SGP combines multiple metal-oxide sensing elements on one chip to provide more detailed air quality signals. This is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
